# Fritzing sketch brewTimer (saved by Fritzing 0.9.3b)
breadboards: 1

parts:
  Part1 = Arduino Uno (Rev3)
  LCD1 = LCD screen
  R1 = Rotary Potentiometer (Small) [maximum_resistance=100kΩ package=THT]
  R2 = Resistor [tolerance=±5% resistance=220 package=THT]
  S1 = Pushbutton [package="[THT]"]
  S2 = Pushbutton [package="[THT]"]
  S3 = Pushbutton [package="[THT]"]
  S4 = Pushbutton [package="[THT]"]
  S5 = Pushbutton [package="[THT]"]
  R3 = Resistor [tolerance=±5% resistance=1k package=THT]
  R5 = Resistor [tolerance=±5% resistance=1k package=THT]
  R6 = Resistor [tolerance=±5% resistance=1k package=THT]
  R7 = Resistor [tolerance=±5% resistance=1k package=THT]
  R8 = Resistor [tolerance=±5% resistance=1k package=THT]
  J1 = Piezo Speaker
  R9 = Resistor [tolerance=±5% resistance=220 package=THT]
  LED1 = RGB LED (com. cathode, rgb) [package="5 mm [THT]"]
  R10 = Resistor [tolerance=±5% resistance=220 package=THT]
  R12 = Rotary Potentiometer (Small) [maximum_resistance=100kΩ package=THT]

nets:
  N1: Part1.A0, LED1.red_anode
  N2: Part1.A1, LED1.green_anode
  N3: Part1.A2, LED1.blue_anode
  N4: Part1.D8, S5.Pin_1, S5.Pin_2, R6.Pin_0
  N5: Part1.D9_PWM, S2.Pin_3, S2.Pin_4, R5.Pin_0
  N6: Part1.D10_PWM/SS, S4.Pin_3, S4.Pin_4, R8.Pin_0
  N7: Part1.D11_PWM/MOSI, S3.Pin_3, S3.Pin_4, R7.Pin_0
  N8: Part1.D12/MISO, S1.Pin_3, S1.Pin_4, R3.Pin_1
  N9: Part1.D2, LCD1.DB7
  N10: Part1.D3_PWM, LCD1.DB6
  N11: Part1.D4, LCD1.DB5
  N12: Part1.D5_PWM, LCD1.DB4
  N13: Part1.D6_PWM, LCD1.E
  N14: Part1.D7, LCD1.RS
  5V: Part1.5V, LCD1.VDD, R1.leg1, R2.Pin_0, S2.Pin_1, S2.Pin_2, S3.Pin_1, S3.Pin_2, S4.Pin_1, S4.Pin_2, S5.Pin_3, S5.Pin_4, R12.leg2
  GND: Part1.GND, LCD1.VSS, LCD1.R/W, LCD1.LED-, R1.leg2, R3.Pin_0, R5.Pin_1, R6.Pin_1, R7.Pin_1, R8.Pin_1, R9.Pin_0, R10.Pin_1, R12.leg1
  N15: LCD1.V0, R1.wiper
  N16: LCD1.LED+, R2.Pin_1
  N17: S1.Pin_1, S1.Pin_2
  N18: J1.pin1, R9.Pin_1
  N19: J1.pin2, R12.wiper
  N20: LED1.common_cathode, R10.Pin_0
