# Fritzing sketch lyskryss (saved by Fritzing 0.9.3b)
breadboards: 1

parts:
  Part1 = Arduino Uno (Rev3)
  R1 = Resistor [tolerance=±5% resistance=220 package=THT]
  LED1 = LED - 5mm [color="Red (633nm)" package="5 mm [THT]"]
  LED2 = LED - 5mm [color="Yellow (585nm)" package="5 mm [THT]"]
  LED3 = LED - 5mm [color="Green (555nm)" package="5 mm [THT]"]
  LED4 = LED - 5mm [color="Red (633nm)" package="5 mm [THT]"]
  LED5 = LED - 5mm [color="Green (555nm)" package="5 mm [THT]"]
  R2 = Resistor [tolerance=±5% resistance=220 package=THT]
  R3 = Resistor [tolerance=±5% resistance=220 package=THT]
  R4 = Resistor [tolerance=±5% resistance=220 package=THT]
  R6 = Resistor [tolerance=±5% resistance=220 package=THT]
  S1 = Pushbutton [package="[THT]"]
  R7 = Resistor [tolerance=±5% resistance=10k package=THT]
  J1 = Basic Servo

nets:
  N1: Part1.D8, LED3.anode
  N2: Part1.D9_PWM, LED2.anode
  N3: Part1.D10_PWM/SS, LED1.anode
  N4: Part1.D2, S1.Pin_1, S1.Pin_2, R7.Pin_0
  N5: Part1.D3_PWM, J1.pulse
  N6: Part1.D6_PWM, LED5.anode
  N7: Part1.D7, LED4.anode
  5V: Part1.5V, S1.Pin_3, S1.Pin_4, J1.vcc
  GND: Part1.GND, R1.Pin_1, R2.Pin_1, R3.Pin_1, R4.Pin_1, R6.Pin_1, R7.Pin_1, J1.gnd
  N8: R1.Pin_0, LED1.cathode
  N9: LED2.cathode, R6.Pin_0
  N10: LED3.cathode, R4.Pin_0
  N11: LED4.cathode, R2.Pin_0
  N12: LED5.cathode, R3.Pin_0
