# Fritzing sketch musikkInstrument (saved by Fritzing 0.9.3b)
breadboards: 1

parts:
  Part1 = Arduino Uno (Rev3)
  S1 = Pushbutton [package="[THT]"]
  S2 = Pushbutton [package="[THT]"]
  S3 = Pushbutton [package="[THT]"]
  S4 = Pushbutton [package="[THT]"]
  S5 = Pushbutton [package="[THT]"]
  S6 = Pushbutton [package="[THT]"]
  R1 = Resistor [tolerance=±5% resistance=220 package=THT]
  R2 = Resistor [tolerance=±5% resistance=470 package=THT]
  R4 = Resistor [tolerance=±5% resistance=1k package=THT]
  R5 = Resistor [tolerance=±5% resistance=2.2k package=THT]
  R6 = Resistor [tolerance=±5% resistance=3.3k package=THT]
  R7 = Rotary Potentiometer (Small) [maximum_resistance=100kΩ package=THT]
  R8 = Rotary Potentiometer (Small) [maximum_resistance=100kΩ package=THT]
  J1 = Piezo Speaker
  Part2 = RFID-RC522-v2
  R9 = Resistor [tolerance=±5% resistance=220 package=THT]

nets:
  N1: Part1.A0, S1.Pin_1, S1.Pin_2, S2.Pin_1, S2.Pin_2, S3.Pin_1, S3.Pin_2, S4.Pin_1, S4.Pin_2, S5.Pin_1, S5.Pin_2, S6.Pin_1, S6.Pin_2
  N2: Part1.A1, R7.wiper
  N3: Part1.D9_PWM, Part2.RST
  N4: Part1.D10_PWM/SS, Part2.SDA
  N5: Part1.D11_PWM/MOSI, Part2.MOSI
  N6: Part1.D12/MISO, Part2.MISO
  N7: Part1.D13/SCK, Part2.SCK
  N8: Part1.D3_PWM, R8.leg1
  N9: Part1.3V3, Part2.3_3V
  N10: Part1.5V, S1.Pin_3, S1.Pin_4, R1.Pin_1, R2.Pin_1, R4.Pin_1, R5.Pin_1, R6.Pin_1, R7.leg1
  GND: Part1.GND, R7.leg2, R8.leg2, J1.pin1, Part2.GND
  N11: S2.Pin_3, S2.Pin_4, R1.Pin_0
  N12: S3.Pin_3, S3.Pin_4, R2.Pin_0
  N13: S4.Pin_3, S4.Pin_4, R4.Pin_0
  N14: S5.Pin_3, S5.Pin_4, R5.Pin_0
  N15: S6.Pin_3, S6.Pin_4, R6.Pin_0
  N16: R8.wiper, R9.Pin_0
  N17: J1.pin2, R9.Pin_1

custom parts:
  RFID-RC522-v2: A simple China made RFID-RC522 Reader; do check the pin labels, as this is a MFRC522 based clone.
